// Logisim project 1part (1).circ as structural Verilog: 1 circuit, main circuit main
module main (
  output out_1,
  output out_2,
  output out_3,
  output out_4,
  output out_5,
  output out_6,
  output out_7,
  output out_8,
  output out_9
);

  wire and_1_out, and_2_out, and_3_out, and_4_out, and_5_out, and_6_out, and_7_out, and_8_out, and_9_out,
       and_10_out, and_11_out, and_12_out, and_13_out, and_14_out, and_15_out, and_16_out, and_17_out,
       and_18_out, and_19_out, and_20_out, and_21_out, and_22_out, and_23_out, and_24_out, and_25_out,
       and_26_out, and_27_out, and_28_out, and_29_out, and_30_out, and_31_out, and_32_out, and_33_out,
       and_34_out, and_35_out, and_36_out, and_37_out, and_38_out, and_39_out, and_40_out, and_41_out,
       and_42_out, and_43_out, and_44_out, and_45_out, and_46_out, and_47_out, and_48_out, and_49_out,
       and_50_out, and_51_out, and_52_out, and_53_out, and_54_out, and_55_out, and_56_out, not_1_out,
       not_2_out, not_3_out, not_4_out, not_5_out, not_6_out, not_7_out, not_8_out, not_9_out, not_10_out,
       not_11_out, not_12_out, not_13_out, not_14_out, not_15_out, not_16_out, not_17_out, not_18_out,
       not_19_out, not_20_out, not_21_out, not_22_out, not_23_out, not_24_out, or_4_out, or_6_out, or_7_out,
       or_9_out, or_11_out, or_13_out, or_15_out;

  not not_1 (not_1_out, 1'b0);
  not not_2 (not_2_out, 1'b0);
  not not_3 (not_3_out, or_4_out);
  and and_1 (and_1_out, 1'b0, 1'b0);
  and and_2 (and_2_out, 1'b0, or_4_out);
  and and_3 (and_3_out, 1'b0, or_4_out);
  and and_4 (and_4_out, 1'b0, not_2_out, not_3_out);
  and and_5 (and_5_out, 1'b0, not_1_out, not_3_out);
  and and_6 (and_6_out, or_4_out, not_1_out, not_2_out);
  and and_7 (and_7_out, 1'b0, 1'b0, or_4_out);
  or or_1 (out_1, and_1_out, and_2_out, and_3_out);
  or or_2 (out_2, and_4_out, and_5_out, and_6_out, and_7_out);
  not not_4 (not_4_out, 1'b0);
  not not_5 (not_5_out, 1'b0);
  not not_6 (not_6_out, or_6_out);
  and and_8 (and_8_out, 1'b0, 1'b0);
  and and_9 (and_9_out, 1'b0, or_6_out);
  and and_10 (and_10_out, 1'b0, or_6_out);
  and and_11 (and_11_out, 1'b0, not_5_out, not_6_out);
  and and_12 (and_12_out, 1'b0, not_4_out, not_6_out);
  and and_13 (and_13_out, or_6_out, not_4_out, not_5_out);
  and and_14 (and_14_out, 1'b0, 1'b0, or_6_out);
  or or_3 (out_3, and_11_out, and_12_out, and_13_out, and_14_out);
  or or_4 (or_4_out, and_8_out, and_9_out, and_10_out);
  not not_7 (not_7_out, 1'b1);
  not not_8 (not_8_out, 1'b0);
  not not_9 (not_9_out, or_7_out);
  and and_15 (and_15_out, 1'b1, 1'b0);
  and and_16 (and_16_out, 1'b1, or_7_out);
  and and_17 (and_17_out, 1'b0, or_7_out);
  and and_18 (and_18_out, 1'b1, not_8_out, not_9_out);
  and and_19 (and_19_out, 1'b0, not_7_out, not_9_out);
  or or_5 (out_4, and_18_out, and_19_out, and_20_out, and_21_out);
  and and_20 (and_20_out, or_7_out, not_7_out, not_8_out);
  and and_21 (and_21_out, 1'b1, 1'b0, or_7_out);
  or or_6 (or_6_out, and_15_out, and_16_out, and_17_out);
  not not_10 (not_10_out, 1'b1);
  not not_11 (not_11_out, 1'b1);
  not not_12 (not_12_out, or_9_out);
  and and_22 (and_22_out, 1'b1, 1'b1);
  and and_23 (and_23_out, 1'b1, or_9_out);
  and and_24 (and_24_out, 1'b1, or_9_out);
  and and_25 (and_25_out, 1'b1, not_11_out, not_12_out);
  and and_26 (and_26_out, 1'b1, not_10_out, not_12_out);
  and and_27 (and_27_out, or_9_out, not_10_out, not_11_out);
  and and_28 (and_28_out, 1'b1, 1'b1, or_9_out);
  or or_7 (or_7_out, and_22_out, and_23_out, and_24_out);
  or or_8 (out_5, and_25_out, and_26_out, and_27_out, and_28_out);
  not not_13 (not_13_out, 1'b0);
  not not_14 (not_14_out, 1'b1);
  not not_15 (not_15_out, or_11_out);
  and and_29 (and_29_out, 1'b0, 1'b1);
  and and_30 (and_30_out, 1'b0, or_11_out);
  and and_31 (and_31_out, 1'b1, or_11_out);
  and and_32 (and_32_out, 1'b0, not_14_out, not_15_out);
  and and_33 (and_33_out, 1'b1, not_13_out, not_15_out);
  and and_34 (and_34_out, or_11_out, not_13_out, not_14_out);
  and and_35 (and_35_out, 1'b0, 1'b1, or_11_out);
  or or_9 (or_9_out, and_29_out, and_30_out, and_31_out);
  or or_10 (out_6, and_32_out, and_33_out, and_34_out, and_35_out);
  not not_16 (not_16_out, 1'b1);
  not not_17 (not_17_out, 1'b1);
  not not_18 (not_18_out, or_13_out);
  and and_36 (and_36_out, 1'b1, 1'b1);
  and and_37 (and_37_out, 1'b1, or_13_out);
  and and_38 (and_38_out, 1'b1, or_13_out);
  and and_39 (and_39_out, 1'b1, not_17_out, not_18_out);
  and and_40 (and_40_out, 1'b1, not_16_out, not_18_out);
  and and_41 (and_41_out, or_13_out, not_16_out, not_17_out);
  and and_42 (and_42_out, 1'b1, 1'b1, or_13_out);
  or or_11 (or_11_out, and_36_out, and_37_out, and_38_out);
  or or_12 (out_7, and_39_out, and_40_out, and_41_out, and_42_out);
  not not_19 (not_19_out, 1'b1);
  not not_20 (not_20_out, or_15_out);
  not not_21 (not_21_out, 1'b0);
  and and_43 (and_43_out, 1'b0, 1'b1);
  and and_44 (and_44_out, 1'b0, or_15_out);
  and and_45 (and_45_out, 1'b1, or_15_out);
  and and_46 (and_46_out, 1'b0, not_19_out, not_20_out);
  and and_47 (and_47_out, 1'b1, not_21_out, not_20_out);
  and and_48 (and_48_out, or_15_out, not_21_out, not_19_out);
  and and_49 (and_49_out, 1'b0, 1'b1, or_15_out);
  or or_13 (or_13_out, and_43_out, and_44_out, and_45_out);
  or or_14 (out_8, and_46_out, and_47_out, and_48_out, and_49_out);
  not not_22 (not_22_out, 1'b0);
  not not_23 (not_23_out, 1'b0);
  not not_24 (not_24_out, 1'b0);
  and and_50 (and_50_out, 1'b0, 1'b0);
  and and_51 (and_51_out, 1'b0, 1'b0);
  and and_52 (and_52_out, 1'b0, 1'b0);
  and and_53 (and_53_out, 1'b0, not_22_out, not_23_out);
  and and_54 (and_54_out, 1'b0, not_24_out, not_23_out);
  and and_55 (and_55_out, 1'b0, not_24_out, not_22_out);
  and and_56 (and_56_out, 1'b0, 1'b0, 1'b0);
  or or_15 (or_15_out, and_50_out, and_51_out, and_52_out);
  or or_16 (out_9, and_53_out, and_54_out, and_55_out, and_56_out);
endmodule
