// Logisim project 3part.circ as structural Verilog: 1 circuit, main circuit main
module main (
  input  in_1,
  input  in_2,
  input  in_3,
  input  in_4,
  input  in_5,
  input  in_6
);

  wire and_1_out, clock_1_out, t_ff_2_q, t_ff_3_q;

  T_Flip_Flop t_ff_1 (.T(and_1_out), .clk(clock_1_out));  // open: Q, Qn, reset, preset
  and and_1 (and_1_out, t_ff_3_q, t_ff_2_q);
  Clock clock_1 (.out(clock_1_out));
  T_Flip_Flop t_ff_2 (.T(t_ff_3_q), .clk(clock_1_out), .Q(t_ff_2_q));  // open: Qn, reset, preset
  T_Flip_Flop t_ff_3 (.T(1'b1), .clk(clock_1_out), .Q(t_ff_3_q));  // open: Qn, reset, preset
  T_Flip_Flop t_ff_4 (.T(in_1), .clk(clock_1_out));  // open: Q, Qn, reset, preset
  S_R_Flip_Flop s_r_ff_1 (.S(in_2), .R(in_3), .clk(clock_1_out));  // open: Q, reset, Qn, preset
  D_Flip_Flop d_ff_1 (.D(in_4), .clk(clock_1_out));  // open: Q, Qn, preset, reset
  J_K_Flip_Flop j_k_ff_1 (.J(in_5), .K(in_6), .clk(clock_1_out));  // open: Q, Qn, preset, reset
endmodule
